# Fritzing sketch schéma (1) (saved by Fritzing 0.8.2b)
breadboards: 1

parts:
  Composants1 = Arduino Uno (Rev3)  # not connected
  R1 = Resistor [tolerance=±5% resistance=10k package=THT]
  DHT22 = Humidity and Temperature Sensor RHT03
  Sonde_PT100 = Temperature Sensor (Thermistor) [thermistor_type=NTC package=THT]
  Q1 = Basic FET N-Channel [package="TO220 [THT]"]
  LED1 = LED - 5mm [color="Red (633nm)" package="5 mm [THT]"]
  J1 = Peltier Element
  R2 = Resistor [tolerance=±5% resistance=10k package=THT]

nets:
  N1: R1.Pin_0, Sonde_PT100.pin_0
  N2: R1.Pin_1, DHT22.Vcc
  N3: DHT22.Data-signal, DHT22.GND_1
  N4: DHT22.GND_2, Sonde_PT100.pin_1, LED1.anode
  N5: Q1.gate, R2.Pin_1
  N6: Q1.drain, J1.pin1
  N7: Q1.source, R2.Pin_0
